# Fritzing sketch doorbell (saved by Fritzing 0.7.5b)
breadboards: 1

parts:
  WeMos_D1_Mini1 = WeMos D1 Mini
  U2 = mystery part, 7 pins [chip_label=RX480R spacing=300mil]
  IC1 = DS1302 [package="DIP8 [THT]"]
  R2 = Resistor [tolerance=±5% resistance=100 package=THT]
  J1 = female pin header, 3 pins [form="♀ (female)"]
  J2 = female pin header, 3 pins [form="♀ (female)"]

nets:
  N1: WeMos_D1_Mini1.3V3, U2.pin2
  N2: WeMos_D1_Mini1.5V, J2.pin3
  N3: WeMos_D1_Mini1.D1, IC1.X2_-_Crystal
  N4: WeMos_D1_Mini1.D2, IC1.+V
  N5: WeMos_D1_Mini1.D5, U2.pin6
  N6: WeMos_D1_Mini1.D6, U2.pin5
  N7: WeMos_D1_Mini1.D7, U2.pin4
  N8: WeMos_D1_Mini1.D8, U2.pin3
  N9: WeMos_D1_Mini1.G, U2.pin1, IC1.CE_-_Chip_Enable, IC1.SCLK_-_SPI_Clock, R2.Pin_1, J2.pin1
  N10: IC1.X1_-_Crystal, IC1.0V, R2.Pin_0
  N11: IC1.I/O_-_SPI_Data_In/Out, J1.pin1
  N12: IC1.Vbat_-_Backup_Supply, J1.pin3
  N13: J1.pin2, J2.pin2

notes:
  Chime Connector
  12V
  C1
  C2
  DS 1302 is actually 2x SSR

custom parts:
  WeMos D1 Mini: The D1 mini is a mini wifi board based on ESP-8266EX.
